# Fritzing sketch LeitorLuminosidade (saved by Fritzing 0.9.2b)
breadboards: 1

parts:
  Componente1 = Arduino Nano (Rev3.0) (ICSP)
  U1 = XBEE-1 [package=xbee-1_lock]
  R1 = Resistor [tolerance=±5% resistance=220 package="0603 [SMD]"]
  R2 = Photocell (LDR) [package=THT]
  U2 = Voltage Regulator [package=to220-adj]
  R3 = Resistor [tolerance=±5% resistance=220 package="0603 [SMD]"]
  R4 = Resistor [tolerance=±5% resistance=220 package="2010 [SMD]"]
  R5 = Resistor [tolerance=±5% resistance=1k package="2010 [SMD]"]
  R6 = Resistor [tolerance=±5% resistance=1k package="0603 [SMD]"]
  R7 = Resistor [tolerance=±5% resistance=1k package="0603 [SMD]"]

nets:
  N1: Componente1.D1/TX, R6.Pin_0
  N2: Componente1.D0/RX, U1.DOUT
  GND: Componente1.GND, U1.GND, R1.Pin_1, R5.Pin_1, R7.Pin_1
  N3: Componente1.VIN, R2.pin_1, U2.OUT
  N4: U1.VDD, U2.IN, R4.Pin_0
  N5: U1.DIN, R6.Pin_1, R7.Pin_0
  N6: R1.Pin_0, R2.pin_0
  N7: U2.ADJ, R3.Pin_0, R5.Pin_0
  N8: R3.Pin_1, R4.Pin_1

notes:
  +5V
  GND
