# Fritzing sketch LeitorTemperatura (saved by Fritzing 0.9.2b)
breadboards: 1

parts:
  U1 = XBEE-1 [package=xbee-1_lock]
  U2 = Voltage Regulator [package=to220-adj]
  R3 = Resistor [tolerance=±5% resistance=220 package="0603 [SMD]"]
  R4 = Resistor [tolerance=±5% resistance=220 package="2010 [SMD]"]
  R5 = Resistor [tolerance=±5% resistance=1k package="2010 [SMD]"]
  R6 = Resistor [tolerance=±5% resistance=1k package="0603 [SMD]"]
  R7 = Resistor [tolerance=±5% resistance=1k package="0603 [SMD]"]
  RHT1 = Humidity and Temperature Sensor RHT03
  Componente1 = Arduino Uno (Rev3) - ICSP
  R8 = Resistor [tolerance=±5% resistance=10k package="1206 [SMD]"]

nets:
  N1: U1.VDD, U2.IN, R4.Pin_0
  N2: U1.DOUT, Componente1.D0/RX
  N3: U1.DIN, R6.Pin_1, R7.Pin_0
  N4: U1.GND, R5.Pin_1, R7.Pin_1, RHT1.GND_2
  N5: U2.ADJ, R3.Pin_0, R5.Pin_0
  N6: U2.OUT, RHT1.Vcc, R8.Pin_1
  N7: R3.Pin_1, R4.Pin_1
  N8: R6.Pin_0, Componente1.D1/TX
  N9: RHT1.Data-signal, Componente1.D8, R8.Pin_0

notes:
  +5V
  GND
